# Fritzing sketch BlinkerModule (saved by Fritzing 0.9.3b)
breadboards: 2

parts:
  부품1 = Arduino Uno (Rev3)
  U1 = 74HC595 [package="DIP16 [THT]"]
  U2 = HEF4543 [package=dil16]
  C1 = Electrolytic Capacitor [capacitance=1μF package="0405 [SMD, electrolytic]"]
  U3 = 7-SEGMENT-DISPLAY [package=7-segment-display]
  U4 = 7-SEGMENT-DISPLAY [package=7-segment-display]
  U5 = 7-SEGMENT-DISPLAY [package=7-segment-display]
  U6 = 7-SEGMENT-DISPLAY [package=7-segment-display]
  R1 = Rotary Potentiometer (Small) [maximum_resistance=100kΩ package=THT]
  R2 = Rotary Potentiometer (Small) [maximum_resistance=100kΩ package=THT]
  LED1 = LED - 5mm [color="Red (633nm)" package="5 mm [THT]"]
  LED3 = LED - 5mm [color="Red (633nm)" package="5 mm [THT]"]

nets:
  N1: 부품1.A0, R1.wiper
  N2: 부품1.A1, R2.wiper
  N3: 부품1.D8, U1.SH_CP
  N4: 부품1.D9_PWM, U1.ST_CP, C1.-
  N5: 부품1.D10_PWM/SS, U1.DS
  N6: 부품1.D11_PWM/MOSI, LED3.anode
  N7: 부품1.D12/MISO, LED1.anode
  VCC: 부품1.5V, U1.MR, U1.VCC, U2.VCC, R1.leg2, R2.leg2
  GND: 부품1.GND, U1.GND, U1.OE, U2.PH, U2.BL, U2.GND, C1.+, U5.C, R1.leg1, R2.leg1, LED1.cathode, LED3.cathode
  N8: U1.Q1, U2.D1
  N9: U1.Q2, U2.D2
  N10: U1.Q3, U2.D3
  N11: U1.Q4, U4.C
  N12: U1.Q5, U3.C
  N13: U1.Q6, U6.C
  N14: U1.Q0, U2.D0
  N15: U2.A, U3.A, U6.A
  N16: U2.B, U3.G2, U6.G2
  N17: U2.C, U3.D, U6.D
  N18: U2.D, U3.G1
  N19: U2.E, U3.DP, U6.DP
  N20: U2.G, U3.E, U6.E
  N21: U2.F, U3.G, U6.G
  N22: U3.B, U6.B
